# Fritzing sketch gsclock_arduino_uno_sketch (saved by Fritzing 0.9.6b)
breadboards: 2

parts:
  パーツ1 = Arduino Uno (Rev3) - ICSP
  Part1 = KY-015 Temperature & Humidity Sensor Module [package="Breakout board"]
  LED1 = LED - 5mm [color="Red (633nm)" current=0.030 package="5 mm [THT]"]
  S1 = Pushbutton [package="[THT]"]
  R3 = Photocell (LDR) [package=THT]
  R4 = Resistor [tolerance=±5% power=0.25 resistance=1k package=THT]
  Pulldown_Regsiter = Resistor [tolerance=±5% power=0.25 resistance=10k package=THT]
  SG1 = Buzzer 12mm [part_number=COM-07950 package=buzzer-12mm-ns]
  R5 = Trimmer Potentiometer [maximum_resistance=10kΩ package=THT]
  LED2 = smd LED [color="Green (555nm)" package="0805 [SMD]"]
  S2 = Pushbutton [package="[THT]"]  # not connected
  Pulldown_Regsiter1 = Resistor [tolerance=±5% power=0.25 resistance=10k package=THT]
  R6 = Resistor [tolerance=±5% power=0.25 resistance=1k package=THT]
  Part2 = KY-022 Infrared Receiver Module [package="Breakout board"]
  LED3 = LED - 5mm [color="Infrared (940nm)" current=0.030 package="5 mm [THT]"]
  LED5 = LED - 5mm [color="Infrared (940nm)" current=0.030 package="5 mm [THT]"]
  R1 = Resistor [tolerance=±5% power=0.25 resistance=1k package=THT]
  R8 = Resistor [tolerance=±5% power=0.25W resistance=10 package=THT]
  LED4 = smd LED [color="Infrared (940nm)" current=0.030 package="0805 [SMD]"]
  HC-SR1 = HC-SR501 Body Sensor Module
  HC-SR04_Sensor_1 = HC-SR04 Ultrasonic Distance Sensor

nets:
  N1: パーツ1.A0, R3.pin_1, R4.Pin_0
  N2: パーツ1.ICSP_MISO, パーツ1.D12/MISO, HC-SR04_Sensor_1.TRIG
  VCC: パーツ1.ICSP_MOSI, パーツ1.D11_PWM/MOSI, パーツ1.D4, Part1.Vin, R3.pin_0, R1.Pin_1, HC-SR1.VCC, HC-SR1.OUT, HC-SR04_Sensor_1.VCC
  N3: パーツ1.D8, R5.leg1
  N4: パーツ1.D9_PWM, R6.Pin_1, Part2.Vin
  N5: パーツ1.D13/SCK, S1.Pin_1, S1.Pin_2, Pulldown_Regsiter.Pin_0
  GND: パーツ1.GND, Part1.-, LED1.cathode, R4.Pin_1, Pulldown_Regsiter.Pin_1, SG1.2, R5.leg2, LED2.cathode, Pulldown_Regsiter1.Pin_1, Part2.-, LED5.cathode, HC-SR1.GND, HC-SR04_Sensor_1.GND
  N6: パーツ1.D2, HC-SR04_Sensor_1.ECHO
  N7: パーツ1.D3_PWM, R8.Pin_1
  N8: パーツ1.D5_PWM, Part2.S
  N9: パーツ1.D7, Part1.S
  N10: パーツ1.5V, S1.Pin_3, S1.Pin_4
  N11: LED1.anode, R1.Pin_0
  N12: SG1.1, R5.wiper
  N13: LED2.anode, R6.Pin_0
  N14: LED3.cathode, LED4.anode
  N15: LED3.anode, R8.Pin_0
  N16: LED5.anode, LED4.cathode

notes:
  jumper cap: H

custom parts:
  KY-015 Temperature & Humidity Sensor Module: DH-11 temperature and humidity sensor in KEYES KY-015 module, provides a low-latency serial interface to measure humidity and temperature.
  Buzzer 12mm: Buzzer 12mm Spark Fun Electronics SKU : Comp-Buzzer Through hole This is a small 12mm round speaker that operates around the audible 2kHz range. You can use these speakers to create simple music or user interfaces. This is not a true piezoelectric speaker but behaves similarly. Instead of a piezoelectric crystal that vibrates with an electric current, this tiny speaker uses an electromagnet to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
  KY-022 Infrared Receiver Module: Arduino IR receiver module KY-022, based on 1838 IR Receiver/Decoder. It reacts to 38kHz infrared light.
  HC-SR501 Body Sensor Module: Pyroelectric Infrared PIR Motion Sensor Detector Module
